# Fritzing sketch CPE301_Assignment04_Parda (saved by Fritzing 0.9.3b)
breadboards: 1

parts:
  Power_Supply = DC Power [voltage=5]
  Power_Supply_2 = DC Power [voltage=5]
  DC_Motor_#71 = DC Motor
  IC1 = ULN2803A [package=THT]
  ATmega328P_Xplained_Mini = atmega328 [package=dip]
  Potentiometer = Rotary Potentiometer (Small) [maximum_resistance=100kΩ package=THT]
  Push_Button = Pushbutton [package="[SMD]"]

nets:
  N1: Power_Supply.V+, ATmega328P_Xplained_Mini.VCC, Potentiometer.leg1
  GND: Power_Supply.V-, Power_Supply_2.V-, IC1.0V, IC1.COM_-_Common, ATmega328P_Xplained_Mini.GND, Potentiometer.leg2, Push_Button.Pin_1, Push_Button.Pin_2
  N2: Power_Supply_2.V+, DC_Motor_#71.pin_2
  N3: DC_Motor_#71.pin_1, IC1.Out_1
  N4: IC1.In_1, ATmega328P_Xplained_Mini.D1_(TX)
  N5: ATmega328P_Xplained_Mini.A0, Potentiometer.wiper
  N6: ATmega328P_Xplained_Mini.A1, Push_Button.Pin_3, Push_Button.Pin_4
