# Fritzing sketch CPE301_Assignment04_Partb (saved by Fritzing 0.9.3b)
breadboards: 1

parts:
  VCC = DC Power [voltage=12V]
  PX243-02AA = Stepper Motor - Unipolar
  Potentiometer_100k = POT [package=pot_alpha_rv16af-20]
  IC1 = ULN2003A [package="SO16 [SMD]"]
  ATmega_Xplained_Mini = atmega328 [package=dip]
  Change_Direction_Push_Button = Pushbutton [package="[THT]"]
  Start_Push_Button = Pushbutton [package="[THT]"]
  VCC_2 = DC Power [voltage=5]

nets:
  N1: VCC.V+, PX243-02AA.COMMON_1, PX243-02AA.COMMON_2, IC1.COM_-_Common
  GND: VCC.V-, Potentiometer_100k.A, ATmega_Xplained_Mini.GND, Change_Direction_Push_Button.Pin_1, Change_Direction_Push_Button.Pin_2, Start_Push_Button.Pin_1, Start_Push_Button.Pin_2, VCC_2.V-
  N2: PX243-02AA.A, IC1.Out_1
  N3: PX243-02AA.C, IC1.Out_2
  N4: PX243-02AA.B, IC1.Out_3
  N5: PX243-02AA.D, IC1.Out_4
  N6: Potentiometer_100k.S, ATmega_Xplained_Mini.A0
  N7: Potentiometer_100k.E, ATmega_Xplained_Mini.VCC, VCC_2.V+
  N8: IC1.In_1, ATmega_Xplained_Mini.D0_(RX)
  N9: IC1.In_2, ATmega_Xplained_Mini.D1_(TX)
  N10: IC1.In_3, ATmega_Xplained_Mini.D2
  N11: IC1.In_4, ATmega_Xplained_Mini.D3_(PWM)
  N12: ATmega_Xplained_Mini.A1, Change_Direction_Push_Button.Pin_3, Change_Direction_Push_Button.Pin_4
  N13: ATmega_Xplained_Mini.A2, Start_Push_Button.Pin_3, Start_Push_Button.Pin_4
