# Fritzing sketch CPE301_Assignment4_PartC (saved by Fritzing 0.9.3b)
breadboards: 1

parts:
  U1 = atmega328 [package=dip]
  J1 = Basic Servo
  R1 = Trimmer Potentiometer [maximum_resistance=10kΩ package=THT]
  V1 = DC Power [voltage=5]
  V2 = DC Power [voltage=5]

nets:
  N1: U1.D1_(TX), J1.pulse
  N2: U1.AVCC, R1.leg1, V1.V+
  GND: U1.GND, J1.gnd, R1.leg2, V2.V-
  N3: U1.A0, R1.wiper
  N4: J1.vcc, V2.V+
